# Fritzing sketch Arduino-ESP8266 (saved by Fritzing 0.9.2b)
breadboards: 1

parts:
  3_3V_PS = Breadboard Power Supply Board SMD
  ESP02 = ESP8266-02 WiFi Module [part_number=ESP8266]
  R1 = Resistor [tolerance=±5% resistance=10k package="0402 [SMD]"]
  R2 = Resistor [tolerance=±5% resistance=10k package="0402 [SMD]"]
  Part2 = Logic Level Converter
  Part1 = Arduino Uno (Rev3) - ICSP
  DHT1 = DHT22 Humidity and Temperature Sensor
  R3 = Resistor [tolerance=±5% resistance=10k package="0402 [SMD]"]

nets:
  GND: 3_3V_PS.GND, ESP02.GND, Part2.GND, Part1.GND, DHT1.GND
  3.3V: 3_3V_PS.VCC, ESP02.VCC, R1.Pin_1, R2.Pin_1, Part2.LV
  9V: 3_3V_PS.VIN
  N1: ESP02.RXD, Part2.TX2_LV
  N2: ESP02.RST, R2.Pin_0
  N3: ESP02.GPIO15, R1.Pin_0
  N4: ESP02.TXD, Part2.RX2_LV
  5V: Part2.HV, Part1.5V, DHT1.VDD, R3.Pin_1
  N5: Part2.RX2_HV, Part1.D1/TX
  N6: Part2.TX2_HV, Part1.D0/RX
  N7: Part1.D7, DHT1.DATA, R3.Pin_0

custom parts:
  ESP8266-02 WiFi Module: Generic WiFi Module based on the ESP8266 with onboard PCB antenna and UART communications
