# Fritzing sketch USB-TTL-ESP8266 (saved by Fritzing 0.9.2b)
breadboards: 1

parts:
  3_3V_PS = Breadboard Power Supply Board SMD
  TTL-USB-UART = FTDI Basic Programmer
  ESP02 = ESP8266-02 WiFi Module [part_number=ESP8266]
  R1 = Resistor [tolerance=±5% resistance=10k package="0402 [SMD]"]
  R2 = Resistor [tolerance=±5% resistance=10k package="0402 [SMD]"]

nets:
  GND: 3_3V_PS.GND, TTL-USB-UART.GND, ESP02.GPIO0, ESP02.GND
  VCC: 3_3V_PS.VCC, ESP02.VCC, R1.Pin_1, R2.Pin_1
  N1: TTL-USB-UART.RXI, ESP02.TXD
  N2: TTL-USB-UART.TXO, ESP02.RXD
  N3: ESP02.RST, R2.Pin_0
  N4: ESP02.GPIO15, R1.Pin_0

custom parts:
  ESP8266-02 WiFi Module: Generic WiFi Module based on the ESP8266 with onboard PCB antenna and UART communications
