# Fritzing sketch Fritzing-DHTxx (saved by Fritzing 0.9.2b)
breadboards: 1

parts:
  Part1 = Arduino Uno (Rev3)
  DHT11_DHT21_or_DHT22 = DHT22 Humidity and Temperature Sensor
  R1 = Resistor [tolerance=±5% resistance=10k package="0603 [SMD]"]

nets:
  GND: Part1.GND, DHT11_DHT21_or_DHT22.GND
  N1: Part1.D7, DHT11_DHT21_or_DHT22.DATA, R1.Pin_0
  5V: Part1.5V, DHT11_DHT21_or_DHT22.VDD, R1.Pin_1
