# Fritzing sketch Fritzing-HCSR04 (saved by Fritzing 0.9.2b)
breadboards: 1

parts:
  Part1 = Arduino Uno (Rev3)
  HC-SR04 = HC-SR04 Ultrasonic Rangemeter

nets:
  GND: Part1.GND, HC-SR04.GND
  N1: Part1.D5_PWM, HC-SR04.Echo
  N2: Part1.D6_PWM, HC-SR04.Trig
  5V: Part1.5V, HC-SR04.VCC
