# Fritzing sketch Fritzing-LM35 (saved by Fritzing 0.9.2b)
breadboards: 1

parts:
  T1 = LM35 Temperature Sensor [package="TO92 [THT]"]
  Part2 = Arduino Uno (Rev3)

nets:
  N1: T1.+Vs, Part2.5V
  N2: T1.Vout, Part2.A0
  GND: T1.GND, Part2.GND
