# Fritzing sketch Fritzing-Resistor-Divider (saved by Fritzing 0.9.2b)
breadboards: 1

parts:
  R1 = PHOTOCELL [package=photocell-kit]
  R2 = Resistor [tolerance=±5% resistance=220 package="2512 [SMD]"]
  Voltmeter1 = Voltmeter
  VCC = 4 x AAA Battery Mount

nets:
  N1: R1.P$1, VCC.+
  N2: R1.P$2, R2.Pin_0, Voltmeter1.Positive
  N3: R2.Pin_1, Voltmeter1.Com, VCC.-

custom parts:
  Voltmeter: A Standard Multimeter in Current mode
