# Fritzing sketch Fritzing-VT93N1 (saved by Fritzing 0.9.2b)
breadboards: 1

parts:
  R2 = Resistor [tolerance=±5% resistance=10k package="2512 [SMD]"]
  R1_(VT93N1) = PHOTOCELL [package=photocell-kit]
  Part1 = Arduino Uno (Rev3)

nets:
  N1: R2.Pin_0, Part1.GND
  N2: R2.Pin_1, R1_(VT93N1).P$1, Part1.A1
  N3: R1_(VT93N1).P$2, Part1.5V
